# Fritzing sketch Week12_motorreverse (saved by Fritzing 0.9.0b)
breadboards: 1

parts:
  Part1 = Arduino Uno (Rev3)
  VCC1 = Battery
  M1 = DC Motor
  Q1 = Basic FET P-Channel [package="TO220 [THT]"]
  D1 = Rectifier Diode [part_number=1N4001 package="300 mil [THT]"]

nets:
  N1: Part1.D11_PWM/MOSI, Q1.gate
  N2: Part1.GND, VCC1.-, Q1.source, D1.anode
  N3: VCC1.+, M1.pin_1
  N4: M1.pin_2, Q1.drain, D1.cathode
