# Fritzing sketch CD74HX4067_MUX (saved by Fritzing 0.9.0b)
breadboards: 1

parts:
  Part1 = Arduino Uno (Rev3)
  U1 = 74HC4067 [package=ssop24]
  U2 = POT [package=pot_alpha_rv16af-20]
  U3 = POT [package=pot_alpha_rv16af-20]
  U4 = POT [package=pot_alpha_rv16af-20]
  U5 = POT [package=pot_alpha_rv16af-20]
  U6 = POT [package=pot_alpha_rv16af-20]
  U7 = POT [package=pot_alpha_rv16af-20]
  U8 = POT [package=pot_alpha_rv16af-20]
  U9 = POT [package=pot_alpha_rv16af-20]
  U10 = POT [package=pot_alpha_rv16af-20]
  U11 = POT [package=pot_alpha_rv16af-20]
  U12 = POT [package=pot_alpha_rv16af-20]
  U14 = POT [package=pot_alpha_rv16af-20]
  R1 = Basic Flex Resistor
  R2 = Resistor [tolerance=±5% resistance=22k package="0805 [SMD]"]
  R3 = PHOTOCELL [package=photocell-kit]
  R4 = PHOTOCELL [package=photocell-kit]
  R6 = Resistor [tolerance=±5% resistance=10k package=THT]
  R7 = Resistor [tolerance=±5% resistance=10k package=THT]
  R8 = PHOTOCELL [package=photocell-kit]
  R9 = Resistor [tolerance=±5% resistance=10k package=THT]

nets:
  N1: Part1.A0, U1.COM
  N2: Part1.D8, U1.S0
  N3: Part1.D9_PWM, U1.S1
  N4: Part1.D10_PWM/SS, U1.S2
  N5: Part1.D11_PWM/MOSI, U1.S3
  5V: Part1.5V, U1.VCC, U10.E, U11.E, U12.E, U14.E, R1.pin_1, R3.P$1, R4.P$1
  N6: Part1.GND, U1.EN, U10.A, U11.A, U12.A, U14.A, R2.Pin_1, R6.Pin_1, R7.Pin_1
  N7: U1.CHAN7, U9.S
  N8: U1.CHAN6, U8.S
  N9: U1.CHAN5, U7.S
  N10: U1.CHAN4, U6.S
  N11: U1.CHAN3, U5.S
  N12: U1.CHAN2, U4.S
  N13: U1.CHAN1, U3.S
  N14: U1.CHAN0, U2.S
  N15: U1.GND, U2.A, U3.A, U4.A, U5.A, U6.A, U7.A, U8.A, U9.A, R9.Pin_1
  N16: U1.CHAN15, R1.Pin_2, R2.Pin_0
  N17: U1.CHAN14, R4.P$2, R7.Pin_0
  N18: U1.CHAN13, R3.P$2, R6.Pin_0
  N19: U1.CHAN12, R8.P$2, R9.Pin_0
  N20: U1.CHAN11, U14.S
  N21: U1.CHAN10, U12.S
  N22: U1.CHAN9, U11.S
  N23: U1.CHAN8, U10.S
  N24: U2.E, U3.E, U4.E, U5.E, U6.E, U7.E, U8.E, U9.E, R8.P$1
