# Fritzing sketch Motor Speed control  (saved by Fritzing 0.9.0b)
breadboards: 1

parts:
  Part1 = Arduino Uno (Rev3)
  R1 = Resistor [tolerance=±5% resistance=220 package=THT]
  Q1 = Basic FET P-Channel [package="TO220 [THT]"]
  Power_plug1 = Power plug
  M1 = DC Motor
  D1 = Rectifier Diode [package="Melf DO-213 AA [SMD]"]

nets:
  N1: Part1.D9_PWM, R1.Pin_0
  GND: Part1.GND, Q1.source, Power_plug1.GND, D1.anode
  N2: R1.Pin_1, Q1.gate
  N3: Q1.drain, M1.pin_2, D1.cathode
  N4: Power_plug1.VCC, M1.pin_1
