# Fritzing sketch Week12_motor (saved by Fritzing 0.9.0b)

parts:
  Part1 = Arduino Uno (Rev3) - ICSP
  Q3 = npn-Powertransistor [package="TO220 [THT]"]
  D1 = Diode [package=diode-1n4001]
  R1 = Resistor [package="2512 [SMD]"]
  VCC1 = Battery block 9V
  M1 = DC Motor

nets:
  N1: Part1.D9_PWM, R1.Pin_0
  N2: Part1.GND, D1.A, VCC1.-
  N3: Q3.collector, D1.C, M1.pin_1
